# Fritzing sketch firegoto (saved by Fritzing 0.8.7b)
circuit board: 14.4288cm x 6.96375cm
breadboards: 1

parts:
  Part1 = Arduino Due (Rev2b)
  DRV_2 = DRV 8825 Stepper Motor Carrier, High Current [part_number="DRV 8825"]
  C1 = Electrolytic Capacitor [capacitance=1µF package="100 mil [THT, electrolytic]"]
  C2 = Electrolytic Capacitor [capacitance=1µF package="100 mil [THT, electrolytic]"]
  DRV_1 = DRV 8825 Stepper Motor Carrier, High Current [part_number="DRV 8825"]
  Power_plug1 = Power plug  # not connected
  M1 = Stepper Motor - Bipolar
  M2 = Stepper Motor - Bipolar
  Part2 = Bluetooth HC-06 Macho
  LED1 = RGB LED (com. anode, rbg) [package="5 mm [THT]"]
  R1 = Resistor [tolerance=±5% resistance=220 package=THT]
  R2 = Resistor [tolerance=±5% resistance=220 package=THT]
  R3 = Resistor [tolerance=±5% resistance=220 package=THT]

nets:
  N1: Part1.D14/TX3, Part2.RXD
  N2: Part1.D15/RX3, Part2.TXD
  5V: Part1.5V, DRV_2.MS1, DRV_1.MS1, Part2.VCC
  N3: Part1.D22, DRV_2.VOLTAGE_ST/_MT
  N4: Part1.D24, DRV_2.GROUND_ST/_MT
  N5: Part1.D26, DRV_2.OUT_2B
  N6: Part1.D28, DRV_2.OUT_2A
  N7: Part1.D30, DRV_2.OUT_1A
  N8: Part1.D32, DRV_2.OUT_1B
  N9: Part1.D34, DRV_2.VOLTAGE_DD
  N10: Part1.D36, DRV_2.GROUND_LOG
  N11: Part1.D38, DRV_1.VOLTAGE_ST/_MT
  N12: Part1.D40, DRV_1.GROUND_ST/_MT
  N13: Part1.D42, DRV_1.OUT_2B
  N14: Part1.D44, DRV_1.OUT_2A
  N15: Part1.D46, DRV_1.OUT_1A
  N16: Part1.D48, DRV_1.OUT_1B
  N17: Part1.D49, R3.Pin_0
  N18: Part1.D50, DRV_1.VOLTAGE_DD
  N19: Part1.D51, R2.Pin_0
  N20: Part1.D52, DRV_1.GROUND_LOG
  N21: Part1.D53, R1.Pin_0
  N22: Part1.GND, C1.-, DRV_1.STEP, LED1.common_anode
  N23: DRV_2.ENABLE, DRV_2.STEP, C2.-, DRV_1.ENABLE, Part2.GND
  N24: DRV_2.MS2, M1.D
  N25: DRV_2.MS3, M1.B
  N26: DRV_2.RESET, M1.C
  N27: DRV_2.SLEEP, M1.A
  N28: DRV_2.DIRECTION, C2.+
  N29: C1.+, DRV_1.DIRECTION
  N30: DRV_1.MS2, M2.D
  N31: DRV_1.MS3, M2.B
  N32: DRV_1.RESET, M2.C
  N33: DRV_1.SLEEP, M2.A
  N34: LED1.red_cathode, R3.Pin_1
  N35: LED1.blue_cathode, R2.Pin_1
  N36: LED1.green_cathode, R1.Pin_1
